# Fritzing sketch esp8266_adapter (saved by Fritzing 0.9.1b)
circuit board: 8.46667cm x 5.64444cm
breadboards: 1

parts:
  J2 = female pin header, 4 pins [form="♀ (female)"]
  R2 = Resistor [tolerance=±5% resistance=220 package=THT]
  R3 = Resistor [tolerance=±5% resistance=220 package=THT]
  J4 = male pin header, 2 pins [form="♂ (male)"]
  R4 = Resistor [tolerance=±5% resistance=220 package=THT]
  R5 = Resistor [tolerance=±5% resistance=220 package=THT]
  C1 = Electrolytic Capacitor [capacitance=1µF package="100 mil [THT, electrolytic]"]
  J3 = female pin header, 4 pins [form="♀ (female)"]
  J6 = male pin header, 3 pins [form="♂ (male)"]
  J5 = male pin header, 5 pins [form="♂ (male)"]
  R6 = Resistor [tolerance=±5% resistance=220 package=THT]
  U1 = V_REG_MIC2920 [package=sot223]
  D1 = Zener Diode [part_number=1N4732A breakdown_voltage=3.6V package="300 mil [THT]"]
  C2 = Ceramic Capacitor [capacitance=100nF package="200 mil [THT, multilayer]"]

nets:
  N1: J2.pin1, J5.pin3
  N2: J2.pin2, R4.Pin_1
  N3: J2.pin3, R5.Pin_1, J5.pin1
  N4: J2.pin4, R2.Pin_1, R3.Pin_1, R4.Pin_0, R5.Pin_0, C1.+, J6.pin2, U1.GND
  N5: R2.Pin_0, J4.pin1, J3.pin3
  N6: R3.Pin_0, J4.pin2, J3.pin2
  N7: C1.-, J3.pin1, J6.pin1, J5.pin4, U1.IN, D1.anode, C2.0
  N8: J3.pin4, R6.Pin_1, D1.cathode
  N9: J6.pin3, J5.pin5, U1.OUT, C2.1
  N10: J5.pin2, R6.Pin_0

notes:
  70Komh x4
  70k x4
  0.1uF
  470uF
  zener 3.3v
  478omh x1
  esp8266 to Arduino board
